// Logisim project 2bit_Encoder.circ as structural Verilog: 1 circuit, main circuit main
module main (
  input  A,
  input  B,
  input  Ctrl
);

  wire and_1_out, and_2_out, not_1_out, or_1_out;

  not not_1 (not_1_out, Ctrl);
  and and_1 (and_1_out, B, not_1_out);
  and and_2 (and_2_out, Ctrl, A);
  or or_1 (or_1_out, and_1_out, and_2_out);
  LED led_1 (.in(or_1_out));
endmodule
