// Logisim project Countdown_3bit_ripple_counter_with_JK_Flip_Flop.circ as structural Verilog: 1 circuit, main circuit main
module main (
  input  in_1,
  input  in_2
);

  wire clock_1_out, j_k_ff_1_q, j_k_ff_2_q, j_k_ff_3_q;

  Clock clock_1 (.out(clock_1_out));
  J_K_Flip_Flop j_k_ff_1 (.J(in_2), .K(in_2), .clk(j_k_ff_2_q), .Q(j_k_ff_1_q), .preset(in_1));  // open: Qn, reset
  LED led_1 (.in(j_k_ff_1_q));
  J_K_Flip_Flop j_k_ff_2 (.J(in_2), .K(in_2), .clk(j_k_ff_3_q), .Q(j_k_ff_2_q), .preset(in_1));  // open: Qn, reset
  LED led_2 (.in(j_k_ff_2_q));
  J_K_Flip_Flop j_k_ff_3 (.J(in_2), .K(in_2), .clk(clock_1_out), .Q(j_k_ff_3_q), .preset(in_1));  // open: Qn, reset
  LED led_3 (.in(j_k_ff_3_q));
endmodule
