// Logisim project JK_Flip_Flop.circ as structural Verilog: 1 circuit, main circuit main
module main (
  input  J,
  input  K
);

  wire clock_1_out, nand_1_out, nand_2_out, nand_3_out, nand_4_out;

  Clock clock_1 (.out(clock_1_out));
  nand nand_1 (nand_1_out, nand_4_out, J, clock_1_out);
  nand nand_2 (nand_2_out, clock_1_out, K, nand_3_out);
  nand nand_3 (nand_3_out, nand_1_out, nand_4_out);
  nand nand_4 (nand_4_out, nand_3_out, nand_2_out);
  LED led_1 (.in(nand_3_out));
  LED led_2 (.in(nand_4_out));

  // Notes on the sheet:
  //   Clock
  //   Q
  //   Q'
endmodule
