// Logisim project Mob_6_counter_using_JK_Flip_Flop.circ as structural Verilog: 1 circuit, main circuit main
module main (
  input  in_1,
  input  in_2
);

  wire and_1_out, and_2_out, clock_1_out;
  wire [2:0] j_k_ff_1_q;

  Clock clock_1 (.out(clock_1_out));
  J_K_Flip_Flop j_k_ff_1 (
    .J(in_1), .K(in_1), .clk(clock_1_out), .Q(j_k_ff_1_q[0]), .reset(and_2_out));  // open: Qn, preset
  LED led_1 (.in(j_k_ff_1_q[0]));
  J_K_Flip_Flop j_k_ff_2 (
    .J(j_k_ff_1_q[0]), .K(j_k_ff_1_q[0]), .clk(clock_1_out), .Q(j_k_ff_1_q[1]), .reset(and_2_out));  // open: Qn, preset
  LED led_2 (.in(j_k_ff_1_q[1]));
  and and_1 (and_1_out, j_k_ff_1_q[0], j_k_ff_1_q[1]);
  J_K_Flip_Flop j_k_ff_3 (
    .J(and_1_out), .K(and_1_out), .clk(clock_1_out), .Q(j_k_ff_1_q[2]), .reset(and_2_out));  // open: Qn, preset
  LED led_3 (.in(j_k_ff_1_q[2]));
  and and_2 (and_2_out, j_k_ff_1_q[2], j_k_ff_1_q[1]);
  Hex_Digit_Display hex_digit_display_1 (.value({in_2, j_k_ff_1_q}));  // open: dp
endmodule
